// Logisim project RV32I_v2.circ as structural Verilog: 5 circuits, main circuit main
module main (
);

  wire alu_1_zero, clk, controller_1_adrsrc, controller_1_irwrote, controller_1_memwrite,
       controller_1_pcwrite, controller_1_regwrite;
  wire [1:0] controller_1_alusrca, controller_1_alusrcb, controller_1_immsrc, controller_1_resultsrc;
  wire [2:0] controller_1_alucontrol;
  wire [31:0] alu_1_result, extender_1_o, multiplexer_1_out, multiplexer_2_out, multiplexer_3_out,
       multiplexer_4_out, ram_1_dout, register_1_q, register_2_q, register_3_q, register_4_q, register_5_q,
       register_6_q, register_7_q, rf_1_rd1, rf_1_rd2;

  Register #(.width(32)) register_1 (
    .D(multiplexer_4_out), .en(controller_1_pcwrite), .clk(clk), .Q(register_1_q));  // open: clr
  Multiplexer #(.width(32)) multiplexer_1 (
    .in0(register_1_q), .in1(multiplexer_4_out), .out(multiplexer_1_out), .sel(controller_1_adrsrc));
  RAM #(.addrWidth(15), .dataWidth(32)) ram_1 (
    .addr(multiplexer_1_out[14:0]), .we(controller_1_memwrite), .oe(1'b1), .clk(clk), .din(register_6_q),
    .dout(ram_1_dout));
  Register #(.width(32)) register_2 (
    .D(register_1_q), .en(controller_1_irwrote), .clk(clk), .Q(register_2_q));  // open: clr
  Register #(.width(32)) register_3 (
    .D(ram_1_dout), .en(controller_1_irwrote), .clk(clk), .Q(register_3_q));  // open: clr
  Register #(.width(32)) register_4 (.D(ram_1_dout), .en(1'b1), .clk(clk), .Q(register_4_q));  // open: clr
  Clock clock_1 (.out(clk));
  Controller controller_1 (
    .Op(register_3_q[6:0]), .in_2(clk), .funct3(register_3_q[14:12]), .funct7(register_3_q[31:25]),
    .Zero(alu_1_zero), .PCWrite(controller_1_pcwrite), .ResultSrc(controller_1_resultsrc),
    .AdrSrc(controller_1_adrsrc), .ALUControl(controller_1_alucontrol), .MemWrite(controller_1_memwrite),
    .ALUSrcA(controller_1_alusrca), .ALUSrcB(controller_1_alusrcb), .IRWrote(controller_1_irwrote),
    .ImmSrc(controller_1_immsrc), .RegWrite(controller_1_regwrite));
  RF rf_1 (
    .CLK(clk), .WD(multiplexer_4_out), .A2(register_3_q[24:20]), .A1(register_3_q[19:15]),
    .A3(register_3_q[11:7]), .We(controller_1_regwrite), .RD1(rf_1_rd1), .RD2(rf_1_rd2));
  extender extender_1 (.ImmSrc(controller_1_immsrc), .in_2(register_3_q[31:7]), .O(extender_1_o));
  Register #(.width(32)) register_5 (.D(rf_1_rd1), .en(1'b1), .clk(clk), .Q(register_5_q));  // open: clr
  Register #(.width(32)) register_6 (.D(rf_1_rd2), .en(1'b1), .clk(clk), .Q(register_6_q));  // open: clr
  Multiplexer #(.select(2), .width(32)) multiplexer_2 (
    .in0(register_1_q), .in1(register_2_q), .in2(register_5_q), .out(multiplexer_2_out),
    .sel(controller_1_alusrca));  // open: in3
  Multiplexer #(.select(2), .width(32)) multiplexer_3 (
    .in0(register_6_q), .in1(extender_1_o), .in2(32'h4), .out(multiplexer_3_out), .sel(controller_1_alusrcb));  // open: in3
  ALU alu_1 (
    .ALUControl(controller_1_alucontrol), .A(multiplexer_2_out), .B(multiplexer_3_out),
    .Result(alu_1_result), .Zero(alu_1_zero));  // open: Negative, Carry, Overflow
  Register #(.width(32)) register_7 (.D(alu_1_result), .en(1'b1), .clk(clk), .Q(register_7_q));  // open: clr
  Multiplexer #(.select(2), .width(32)) multiplexer_4 (
    .in0(register_7_q), .in1(register_4_q), .in2(alu_1_result), .out(multiplexer_4_out),
    .sel(controller_1_resultsrc));  // open: in3
endmodule

module extender (
  input  [1:0] ImmSrc,
  input  [24:0] in_2,
  output [31:0] O
);

  wire undriven;
  wire [19:0] demultiplexer_1_out0;
  wire [31:0] bit_extender_1_out, bit_extender_2_out, bit_extender_3_out, bit_extender_4_out,
       bit_extender_5_out;

  Demultiplexer #(.width(20)) demultiplexer_1 (
    .out0(demultiplexer_1_out0), .out1(in_2[24:5]), .sel(undriven));  // open: in
  assign bit_extender_1_out = {{20{in_2[24]}}, in_2[24:13]};  // Bit_Extender bit_extender_1
  assign bit_extender_2_out = {{20{in_2[24]}}, {in_2[24:18], in_2[4:0]}};  // Bit_Extender bit_extender_2
  assign bit_extender_3_out = {{20{in_2[24]}}, {in_2[24], in_2[0], in_2[23:18], in_2[4:1]}};  // Bit_Extender bit_extender_3
  assign bit_extender_4_out = {{12{demultiplexer_1_out0[19]}}, demultiplexer_1_out0};  // Bit_Extender bit_extender_4
  assign bit_extender_5_out = {{12{in_2[24]}}, {in_2[24], in_2[12:5], in_2[13], in_2[23:14]}};  // Bit_Extender bit_extender_5
  Multiplexer #(.select(2), .width(32)) multiplexer_1 (
    .in0(bit_extender_1_out), .in1(bit_extender_2_out), .in2(bit_extender_3_out), .in3(bit_extender_5_out),
    .out(O), .sel(ImmSrc));
endmodule

module ALU (
  input  [2:0] ALUControl,
  input  [31:0] A,
  input  [31:0] B,
  output [31:0] Result,
  output Zero,
  output Negative,
  output Carry,
  output Overflow
);

  wire adder_1_cout, not_2_out, S31, xnor_1_out, xor_1_out;
  wire [30:0] adder_1_out;
  wire [31:0] and_1_out, multiplexer_1_out, not_1_out, or_1_out;

  assign not_1_out = ~B;  // NOT_Gate not_1, 32 bits wide
  Multiplexer #(.width(32)) multiplexer_1 (.in0(B), .in1(not_1_out), .out(multiplexer_1_out), .sel(ALUControl[0]));
  not not_2 (not_2_out, ALUControl[2]);
  xor xor_1 (xor_1_out, S31, A[31]);
  NotExactlyOne xnor_1 (.out(xnor_1_out), .in0(B[31]), .in1(A[31]), .in2(ALUControl[0]));
  Adder #(.width(32)) adder_1 (
    .a(multiplexer_1_out), .b(A), .out({S31, adder_1_out}), .cin(ALUControl[0]), .cout(adder_1_cout));
  assign and_1_out = B & A;  // AND_Gate and_1, 32 bits wide
  assign or_1_out = B | A;  // OR_Gate or_1, 32 bits wide
  and and_2 (Carry, adder_1_cout, not_2_out);
  Multiplexer #(.select(2), .width(32)) multiplexer_2 (
    .in0({S31, adder_1_out}), .in1({S31, adder_1_out}), .in2(and_1_out), .in3(or_1_out),
    .out({Negative, Result[30:0]}), .sel(ALUControl[2:1]));
  and and_3 (Overflow, not_2_out, xor_1_out, xnor_1_out);
  Comparator #(.width(32)) comparator_1 (.a({Negative, Result[30:0]}), .b({32{1'b0}}), .eq(Zero));  // open: gt, lt

  assign Result[31] = Negative;

  // Other names for the same wires on the sheet: alu1 = ALUControl[2]; R[31:0] = {Negative, Result[30:0]}
endmodule

module RF (
  input  CLK,
  input  [31:0] WD,
  input  [4:0] A2,
  input  [4:0] A1,
  input  [4:0] A3,
  input  We,
  output [31:0] RD1,
  output [31:0] RD2
);

  wire decoder_1_out0, decoder_1_out1, w1, w2, w3, w4, w5, w6, w7, w8, w9, w10, w11, w12, w13, w14, w15, w16,
       w17, w18, w19, w20, w21, w22, w23, w24, w25, w26, w27, w28, w29, w30, w31;
  wire [31:0] multiplexer_1_out, multiplexer_2_out, multiplexer_4_out, multiplexer_5_out, x0, x1, x2, x3, x4,
       x5, x6, x7, x8, x9, x10, x11, x12, x13, x14, x15, x16, x17, x18, x19, x20, x21, x22, x23, x24, x25,
       x26, x27, x28, x29, x30, x31;

  Register #(.width(32)) register_1 (.D(WD), .en(1'b0), .clk(CLK), .Q(x0));  // open: clr
  Register #(.width(32)) register_2 (.D(WD), .en(w31), .clk(CLK), .Q(x31));  // open: clr
  Register #(.width(32)) register_3 (.D(WD), .en(w1), .clk(CLK), .Q(x1));  // open: clr
  Register #(.width(32)) register_4 (.D(WD), .en(w2), .Q(x2));  // open: clk, clr
  Register #(.width(32)) register_5 (.D(WD), .en(w3), .clk(CLK), .Q(x3));  // open: clr
  Register #(.width(32)) register_6 (.D(WD), .en(w4), .clk(CLK), .Q(x4));  // open: clr
  Register #(.width(32)) register_7 (.D(WD), .en(w5), .clk(CLK), .Q(x5));  // open: clr
  Register #(.width(32)) register_8 (.D(WD), .en(w6), .clk(CLK), .Q(x6));  // open: clr
  Register #(.width(32)) register_9 (.D(WD), .en(w7), .clk(CLK), .Q(x7));  // open: clr
  Register #(.width(32)) register_10 (.D(WD), .en(w8), .clk(CLK), .Q(x8));  // open: clr
  Register #(.width(32)) register_11 (.D(WD), .en(w9), .clk(CLK), .Q(x9));  // open: clr
  Register #(.width(32)) register_12 (.D(WD), .en(w10), .clk(CLK), .Q(x10));  // open: clr
  Register #(.width(32)) register_13 (.D(WD), .en(w11), .clk(CLK), .Q(x11));  // open: clr
  Register #(.width(32)) register_14 (.D(WD), .en(w12), .clk(CLK), .Q(x12));  // open: clr
  Register #(.width(32)) register_15 (.D(WD), .en(w13), .clk(CLK), .Q(x13));  // open: clr
  Register #(.width(32)) register_16 (.D(WD), .en(w14), .clk(CLK), .Q(x14));  // open: clr
  Register #(.width(32)) register_17 (.D(WD), .en(w15), .clk(CLK), .Q(x15));  // open: clr
  Register #(.width(32)) register_18 (.D(WD), .en(w16), .clk(CLK), .Q(x16));  // open: clr
  Register #(.width(32)) register_19 (.D(WD), .en(w17), .clk(CLK), .Q(x17));  // open: clr
  Register #(.width(32)) register_20 (.D(WD), .en(w18), .clk(CLK), .Q(x18));  // open: clr
  Register #(.width(32)) register_21 (.D(WD), .en(w19), .clk(CLK), .Q(x19));  // open: clr
  Register #(.width(32)) register_22 (.D(WD), .en(w20), .clk(CLK), .Q(x20));  // open: clr
  Multiplexer #(.select(4), .width(32)) multiplexer_1 (
    .in0(x0), .in1(x1), .in2(x2), .in3(x3), .in4(x4), .in5(x5), .in6(x6), .in7(x7), .in8(x8), .in9(x9),
    .in10(x10), .in11(x11), .in12(x12), .in13(x13), .in14(x14), .in15(x15), .out(multiplexer_1_out));  // open: sel
  Multiplexer #(.select(4), .width(32)) multiplexer_2 (
    .in0(x16), .in1(x17), .in2(x18), .in3(x19), .in4(x20), .in5(x21), .in6(x22), .in7(x23), .in8(x24),
    .in9(x25), .in10(x26), .in11(x27), .in12(x28), .in13(x29), .in14(x30), .in15(x31),
    .out(multiplexer_2_out), .sel(A1[3:0]));
  Decoder decoder_1 (.out0(decoder_1_out0), .out1(decoder_1_out1), .sel(A3[4]), .en(We));
  Register #(.width(32)) register_23 (.D(WD), .en(w21), .clk(CLK), .Q(x21));  // open: clr
  Register #(.width(32)) register_24 (.D(WD), .en(w22), .clk(CLK), .Q(x22));  // open: clr
  Register #(.width(32)) register_25 (.D(WD), .en(w23), .clk(CLK), .Q(x23));  // open: clr
  Register #(.width(32)) register_26 (.D(WD), .en(w24), .clk(CLK), .Q(x24));  // open: clr
  Register #(.width(32)) register_27 (.D(WD), .en(w25), .clk(CLK), .Q(x25));  // open: clr
  Register #(.width(32)) register_28 (.D(WD), .en(w26), .clk(CLK), .Q(x26));  // open: clr
  Register #(.width(32)) register_29 (.D(WD), .en(w27), .clk(CLK), .Q(x27));  // open: clr
  Register #(.width(32)) register_30 (.D(WD), .en(w28), .clk(CLK), .Q(x28));  // open: clr
  Register #(.width(32)) register_31 (.D(WD), .en(w29), .clk(CLK), .Q(x29));  // open: clr
  Register #(.width(32)) register_32 (.D(WD), .en(w30), .clk(CLK), .Q(x30));  // open: clr
  Multiplexer #(.width(32)) multiplexer_3 (.in0(multiplexer_1_out), .in1(multiplexer_2_out), .out(RD1), .sel(A1[4]));
  Decoder #(.select(4)) decoder_2 (
    .out1(w1), .out2(w2), .out3(w3), .out4(w4), .out5(w5), .out6(w6), .out7(w7), .out8(w8), .out9(w9),
    .out10(w10), .out11(w11), .out12(w12), .out13(w13), .out14(w14), .out15(w15), .sel(A3[3:0]),
    .en(decoder_1_out0));  // open: out0
  Decoder #(.select(4)) decoder_3 (
    .out0(w16), .out1(w17), .out2(w18), .out3(w19), .out4(w20), .out5(w21), .out6(w22), .out7(w23),
    .out8(w24), .out9(w25), .out10(w26), .out11(w27), .out12(w28), .out13(w29), .out14(w30), .out15(w31),
    .sel(A3[3:0]), .en(decoder_1_out1));
  Multiplexer #(.select(4), .width(32)) multiplexer_4 (
    .in0(x0), .in1(x1), .in2(x2), .in3(x3), .in4(x4), .in5(x5), .in6(x6), .in7(x7), .in8(x8), .in9(x9),
    .in10(x10), .in11(x11), .in12(x12), .in13(x13), .in14(x14), .in15(x15), .out(multiplexer_4_out));  // open: sel
  Multiplexer #(.select(4), .width(32)) multiplexer_5 (
    .in0(x16), .in1(x17), .in2(x18), .in3(x19), .in4(x20), .in5(x21), .in6(x22), .in7(x23), .in8(x24),
    .in9(x25), .in10(x26), .in11(x27), .in12(x28), .in13(x29), .in14(x30), .in15(x31),
    .out(multiplexer_5_out), .sel(A2[3:0]));
  Multiplexer #(.width(32)) multiplexer_6 (.in0(multiplexer_4_out), .in1(multiplexer_5_out), .out(RD2), .sel(A2[4]));
endmodule

module Controller (
  input  [6:0] Op,
  input  in_2,
  input  [2:0] funct3,
  input  [6:0] funct7,
  input  Zero,
  output PCWrite,
  output [1:0] ResultSrc,
  output AdrSrc,
  output [2:0] ALUControl,
  output MemWrite,
  output [1:0] ALUSrcA,
  output [1:0] ALUSrcB,
  output IRWrote,
  output [1:0] ImmSrc,
  output RegWrite
);

  wire Brc, PCup;
  wire [1:0] ALUOp;
  wire [2:0] multiplexer_1_out, multiplexer_2_out, multiplexer_3_out, multiplexer_4_out, multiplexer_5_out,
       undriven;
  wire [3:0] multiplexer_7_out, multiplexer_8_out, multiplexer_9_out, multiplexer_10_out, multiplexer_11_out,
       multiplexer_12_out, register_1_q;
  wire [18:14] rom_1_data;

  Register #(.width(4)) register_1 (.D(multiplexer_7_out), .en(1'b1), .clk(in_2), .Q(register_1_q));  // open: clr
  Multiplexer #(.width(3)) multiplexer_1 (.in0(3'b100), .in1(3'b011), .out(multiplexer_1_out), .sel(funct3[0]));
  ROM #(.addrWidth(4), .dataWidth(19)) rom_1 (
    .addr(register_1_q),
    .data({rom_1_data, ALUOp, AdrSrc, ALUSrcB, ALUSrcA, ResultSrc, IRWrote, MemWrite, RegWrite, PCup, Brc}));
  Multiplexer #(.width(3)) multiplexer_2 (.in0(3'b000), .in1(3'b001), .out(multiplexer_2_out), .sel(funct7[5]));
  Multiplexer #(.width(3)) multiplexer_3 (
    .in1(multiplexer_1_out), .out(multiplexer_3_out), .sel(funct3[1]));  // open: in0
  Multiplexer #(.width(3)) multiplexer_4 (
    .in0(multiplexer_2_out), .in1(undriven), .out(multiplexer_4_out), .sel(funct3[0]));
  Multiplexer #(.width(3)) multiplexer_5 (
    .in0(multiplexer_4_out), .in1(multiplexer_3_out), .out(multiplexer_5_out), .sel(funct3[2]));
  Multiplexer #(.select(2), .width(3)) multiplexer_6 (
    .in0(3'b000), .in1(3'b001), .in2(multiplexer_5_out), .out(ALUControl), .sel(ALUOp));  // open: in3
  Multiplexer #(.width(4)) multiplexer_7 (
    .in0(rom_1_data[17:14]), .in1(multiplexer_11_out), .out(multiplexer_7_out), .sel(rom_1_data[18]));
  Multiplexer #(.width(4)) multiplexer_8 (
    .in0(multiplexer_9_out), .in1(4'b0010), .out(multiplexer_8_out), .sel(rom_1_data[14]));
  Multiplexer #(.width(4)) multiplexer_9 (.in0(4'b0011), .in1(4'b0101), .out(multiplexer_9_out), .sel(Op[5]));
  Multiplexer #(.width(4)) multiplexer_10 (.in0(4'b1000), .in1(4'b0110), .out(multiplexer_10_out), .sel(Op[5]));
  Multiplexer #(.select(2), .width(4)) multiplexer_11 (
    .in0(multiplexer_8_out), .in1(multiplexer_10_out), .in2(multiplexer_12_out), .out(multiplexer_11_out),
    .sel({Op[6], Op[4]}));  // open: in3
  Multiplexer #(.width(4)) multiplexer_12 (.in0(4'b1010), .in1(4'b1001), .out(multiplexer_12_out), .sel(Op[3]));

  // Other names for the same wires on the sheet: RW = RegWrite; irw = IRWrote; aluSA[1:0] = ALUSrcA;
  //   aluSB[1:0] = ALUSrcB; aluC[2:0] = ALUControl; clk = in_2; immS[1:0] = ImmSrc; pcw = PCWrite

  // Notes on the sheet:
  //   contents of rom_1 (hex, n*v repeats v):
  //   4452 7c280 78300 10800 24 808 1e100 4 1e300 1c482 1101
endmodule
